# Fritzing sketch schematic (saved by Fritzing 0.9.2b)
circuit board: 7.26531cm x 8.10798cm
breadboards: 1

parts:
  Part1 = Arduino Pro Mini v13
  Part2 = USB LiPoly Charger
  Part3 = Power Cell LiPo Charger/Booster
  J1 = Piezo Speaker
  U4 = TRANSISTOR_NPN_2 [package=to-92]
  U5 = LIPO-2000mAh [package=lipo-2000]
  R1 = Resistor [tolerance=±5% resistance=220 package="0805 [SMD]"]
  U6 = BMP085 Pressure Sensor [package=bmp085]
  JP1 = Header 6 [package=molex-1x6-ra]
  JP2 = Header 8 [package=bm08b-srss-tb]

nets:
  N1: Part1.VCC, U6.VDDD, JP1.5, JP2.6
  GND: Part1.GND, U6.GND, JP1.6, JP2.8
  N2: Part1.A4, U6.SDA
  N3: Part1.A5, U6.SCL
  N4: Part1.RAW, Part1.A1, Part2.VBAT, U5.-
  N5: Part1.A0, JP2.7
  N6: Part1.D13/SCK, JP1.2
  N7: Part1.D12/MISO, JP1.3
  N8: Part1.D11_PWM/MOSI, JP1.4
  N9: Part1.D10_PWM/SS, JP1.1
  N10: Part1.D7, JP2.5
  N11: Part1.D6_PWM, JP2.4
  N12: Part1.D5_PWM, JP2.3
  N13: Part1.D4, JP2.2
  N14: Part1.D3_PWM, JP2.1
  N15: Part1.D2, R1.Pin_0
  GND_2: Part2.GND, Part3.GND, U4.E, U5.+
  N16: Part3.VBATT, J1.pin1
  N17: J1.pin2, U4.C
  N18: U4.B, R1.Pin_1
