# Fritzing sketch schematic_bk (saved by Fritzing 0.9.2b)
breadboards: 1

parts:
  Part1 = Arduino Pro Mini v13
  J1 = Piezo Speaker
  U4 = TRANSISTOR_NPN_2 [package=to-92]
  U5 = LIPO-2000mAh [package=lipo-2000]
  R1 = Resistor [tolerance=±5% resistance=220 package="0805 [SMD]"]
  U6 = BMP085 Pressure Sensor [package=bmp085]
  JP1 = Header 6 [package=molex-1x6-ra]
  U7 = ADMP504 - Ultralow Noise Microphone with Bottom Port and Analog Output [part_number=ADMP504]
  Part2 = USB LiPoly Charger
  Nokia_5110_LCD_Module1 = Nokia 5110 LCD basado en PCD8544

nets:
  VCC: Part1.VCC, U6.VDDD, JP1.5, Nokia_5110_LCD_Module1.VCC
  GND: Part1.GND, U6.GND, JP1.6, Nokia_5110_LCD_Module1.GND
  N1: Part1.A4, U6.SDA
  N2: Part1.A5, U6.SCL
  N3: Part1.RAW, U7.VDD
  N4: Part1.A0, Nokia_5110_LCD_Module1.BL
  N5: Part1.D13/SCK, JP1.2
  N6: Part1.D12/MISO, JP1.3
  N7: Part1.D11_PWM/MOSI, JP1.4
  N8: Part1.D10_PWM/SS, JP1.1
  N9: Part1.D7, Nokia_5110_LCD_Module1.SCL
  N10: Part1.D6_PWM, Nokia_5110_LCD_Module1.DIN
  N11: Part1.D5_PWM, Nokia_5110_LCD_Module1.DC
  N12: Part1.D4, Nokia_5110_LCD_Module1.CE
  N13: Part1.D3_PWM, Nokia_5110_LCD_Module1.RST
  N14: Part1.D2, R1.Pin_0
  N15: J1.pin2, U4.C
  N16: U4.B, R1.Pin_1
  N17: U4.E, U5.+, U7.OUTPUT, U7.NC, Part2.GND
  N18: U5.-, U7.GND, Part2.VBAT

custom parts:
  Nokia 5110 LCD basado en PCD8544: Módulo Nokia 5110 LCD basado en el controlador PCD8544. Versión de 8 pines (sólo entrada).
